// Logisim project processor.circ as structural Verilog: 8 circuits, main circuit RegisterFile
module main (
);

  wire alu_1_eq_flag, alu_1_gr_flag, alu_1_sm_flag, and_1_out, and_2_out, and_3_out, clock_1_out, CMP_FLAG,
       irdecoder_1_lit_flag, not_1_out, or_1_out, or_2_out, RESET, STAGE_EXEC, STAGE_FETCH, STAGE_STORE,
       STOP, USE_ALU_OUTPUT, USE_MEM_OUTPUT, WRITE_MEM, WRITE_PC, WRITE_REG;
  wire [2:0] irdecoder_1_reg1, irdecoder_1_reg2;
  wire [7:0] irdecoder_1_op_code;
  wire [15:0] adder_1_out, alu_1_alu_out, IR_q, multiplexer_1_out, multiplexer_2_out, multiplexer_3_out,
       multiplexer_4_out, multiplexer_5_out, PC_q, ram_1_dout, Registers_ra, Registers_rb, rom_1_p3, rom_1_p4;

  Clock clock_1 (.out(clock_1_out));
  Button button_1 (.out(RESET));
  LED led_1 (.in(STOP));
  and and_1 (and_1_out, WRITE_PC, CMP_FLAG);
  and and_2 (and_2_out, clock_1_out, not_1_out);
  not not_1 (not_1_out, STOP);
  Register #(.width(16)) PC (.D(multiplexer_1_out), .en(1'b1), .clk(STAGE_STORE), .Q(PC_q), .clr(RESET));
  Multiplexer #(.width(16)) multiplexer_1 (
    .in0(adder_1_out), .in1(multiplexer_3_out), .out(multiplexer_1_out), .sel(and_1_out));
  Pull_Resistor pull_resistor_1 (.node(RESET));
  Register #(.width(1)) register_1 (.D(or_1_out), .en(1'b1), .clk(or_2_out), .Q(STAGE_FETCH));  // open: clr
  or or_1 (or_1_out, RESET, STAGE_STORE);
  or or_2 (or_2_out, and_2_out, RESET);
  Adder #(.width(16)) adder_1 (.a(PC_q), .b(multiplexer_2_out), .out(adder_1_out));  // open: cin, cout
  Multiplexer #(.width(16)) multiplexer_2 (
    .in0(16'h1), .in1(16'h2), .out(multiplexer_2_out), .sel(irdecoder_1_lit_flag));
  // ROM #(.addrWidth(16), .dataWidth(16), .line("dual"), .misaligned("true")) rom_1: pin names not known; wires that end beside it: PC_q, STAGE_EXEC, rom_1_p3, rom_1_p4
  Register #(.width(1)) register_2 (.D(STAGE_FETCH), .en(1'b1), .clk(or_2_out), .Q(STAGE_STORE), .clr(RESET));
  Register #(.width(1)) register_3 (.D(STAGE_STORE), .en(1'b1), .clk(or_2_out), .Q(STAGE_EXEC), .clr(RESET));
  Register #(.trigger("high"), .width(16)) IR (.D(rom_1_p3), .en(1'b1), .clk(STAGE_FETCH), .Q(IR_q), .clr(RESET));
  // Probe on rom_1_p4
  PLA #(.in_width(8), .out_width(1), .\table ("11111111 1 # stop instruction")) pla_1 (
    .in(irdecoder_1_op_code), .out(STOP));
  PLA #(.in_width(8), .out_width(1), .\table ("01000xxx 1 # JMP")) pla_2 (.in(irdecoder_1_op_code), .out(WRITE_PC));
  PLA #(.in_width(8), .out_width(1), .\table ("00000010 1 # MOVE\n00000100 1 # LOAD\n00010xxx 0 # INT ALU\n00100000 1 # FLOAT ALU\n01000xxx 1 # LOGIC ALU")) pla_3 (
    .in(irdecoder_1_op_code), .out(WRITE_REG));
  PLA #(.in_width(8), .out_width(1), .\table ("00000011 1 # STORE")) pla_4 (.in(irdecoder_1_op_code), .out(WRITE_MEM));
  PLA #(.in_width(8), .out_width(1), .\table ("00000100 1 # LOAD")) pla_5 (
    .in(irdecoder_1_op_code), .out(USE_MEM_OUTPUT));
  PLA #(.in_width(8), .out_width(1), .\table ("00010xxx 1 # INT ALU\n00100xxx 1 # FLOAT ALU\n01000xxx 1 # LOGIC ALU")) pla_6 (
    .in(irdecoder_1_op_code), .out(USE_ALU_OUTPUT));
  IRDecoder irdecoder_1 (
    .INST(IR_q), .OP_CODE(irdecoder_1_op_code), .REG1(irdecoder_1_reg1), .REG2(irdecoder_1_reg2),
    .LIT_FLAG(irdecoder_1_lit_flag));
  and and_3 (and_3_out, STAGE_STORE, WRITE_REG);
  RegisterFile Registers (
    .RESET(RESET), .CLOCK(and_2_out), .WRITE_STAGE(and_3_out), .RA_SELECT(irdecoder_1_reg1),
    .RB_SELECT(irdecoder_1_reg2), .WRITE_VAL(multiplexer_5_out), .RA(Registers_ra), .RB(Registers_rb));
  // Probe on Registers_ra
  Multiplexer #(.width(16)) multiplexer_3 (
    .in0(Registers_rb), .in1(rom_1_p4), .out(multiplexer_3_out), .sel(irdecoder_1_lit_flag));
  RAM #(.addrWidth(16), .dataWidth(16)) ram_1 (
    .addr(Registers_ra), .we(WRITE_MEM), .clk(STAGE_STORE), .din(multiplexer_3_out), .dout(ram_1_dout));  // open: oe
  ALU alu_1 (
    .INPUT_1(Registers_ra), .INPUT_2(multiplexer_3_out), .CLOCK(STAGE_STORE), .OP_CODE(irdecoder_1_op_code),
    .ALU_OUT(alu_1_alu_out), .GR_FLAG(alu_1_gr_flag), .EQ_FLAG(alu_1_eq_flag), .SM_FLAG(alu_1_sm_flag));
  Multiplexer #(.width(16)) multiplexer_4 (
    .in0(ram_1_dout), .in1(alu_1_alu_out), .out(multiplexer_4_out), .sel(USE_ALU_OUTPUT));
  Multiplexer #(.width(16)) multiplexer_5 (
    .in0(multiplexer_4_out), .in1(rom_1_p4), .out(multiplexer_5_out), .sel(irdecoder_1_lit_flag));
  CMPFlagSelector cmpflagselector_1 (
    .GR_FLAG(alu_1_gr_flag), .EQ_FLAG(alu_1_eq_flag), .SM_FLAG(alu_1_sm_flag), .OP_CODE(irdecoder_1_op_code),
    .FLAG(CMP_FLAG));

  // Notes on the sheet:
  //   contents of rom_1 (hex, n*v repeats v):
  //   202 c000 302 cdef 420 1120 1802 f000 4002 0 ffff
endmodule

module RegisterFile (
  input  [15:0] WRITE_VAL,
  input  WRITE_STAGE,
  input  [2:0] RA_SELECT,
  input  [2:0] RB_SELECT,
  input  RESET,
  input  CLOCK,
  output [15:0] RA,
  output [15:0] RB
);

  wire demultiplexer_1_out0, demultiplexer_1_out1, demultiplexer_1_out2, demultiplexer_1_out3,
       demultiplexer_1_out4, demultiplexer_1_out5, demultiplexer_1_out6, demultiplexer_1_out7;
  wire [15:0] A_q, B_q, C_q, D_q, E_q, F_q, G_q, H_q, register_2_q;

  Pull_Resistor pull_resistor_1 (.node(WRITE_STAGE));
  Demultiplexer #(.enable("true"), .select(3)) demultiplexer_1 (
    .out0(demultiplexer_1_out0), .out1(demultiplexer_1_out1), .out2(demultiplexer_1_out2),
    .out3(demultiplexer_1_out3), .out4(demultiplexer_1_out4), .out5(demultiplexer_1_out5),
    .out6(demultiplexer_1_out6), .out7(demultiplexer_1_out7), .in(WRITE_STAGE), .sel(RA_SELECT));  // open: en
  Register #(.width(16)) A (.D(WRITE_VAL), .clk(demultiplexer_1_out0), .Q(A_q), .clr(RESET));  // open: en
  Register #(.width(16)) B (.D(WRITE_VAL), .clk(demultiplexer_1_out1), .Q(B_q), .clr(RESET));  // open: en
  Register #(.width(16)) C (.D(WRITE_VAL), .clk(demultiplexer_1_out2), .Q(C_q), .clr(RESET));  // open: en
  Register #(.width(16)) D (.D(WRITE_VAL), .clk(demultiplexer_1_out3), .Q(D_q), .clr(RESET));  // open: en
  Register #(.width(16)) E (.D(WRITE_VAL), .clk(demultiplexer_1_out4), .Q(E_q), .clr(RESET));  // open: en
  Register #(.width(16)) F (.D(WRITE_VAL), .clk(demultiplexer_1_out5), .Q(F_q), .clr(RESET));  // open: en
  Register #(.width(16)) G (.D(WRITE_VAL), .clk(demultiplexer_1_out6), .Q(G_q), .clr(RESET));  // open: en
  Register #(.width(16)) H (.D(WRITE_VAL), .clk(demultiplexer_1_out7), .Q(H_q), .clr(RESET));  // open: en
  Multiplexer #(.select(3), .width(16)) multiplexer_1 (
    .in0(A_q), .in1(B_q), .in2(C_q), .in3(D_q), .in4(E_q), .in5(F_q), .in6(G_q), .in7(H_q), .out(RA),
    .sel(RA_SELECT));
  Register #(.width(16)) register_1 (.D(RA), .en(1'b1), .clk(CLOCK));  // open: Q, clr
  Multiplexer #(.select(3), .width(16)) multiplexer_2 (
    .in0(A_q), .in1(B_q), .in2(C_q), .in3(D_q), .in4(E_q), .in5(F_q), .in6(G_q), .in7(H_q), .out(RB),
    .sel(RB_SELECT));
  Register #(.width(16)) register_2 (.D(RB), .en(1'b1), .clk(CLOCK), .Q(register_2_q));  // open: clr
endmodule

module IRSelector (
  input  [23:0] IR_input,
  output [4:0] OP_code,
  output [2:0] Register1,
  output [2:0] Register2,
  output [15:0] Liter
);

  wire [5:0] bitselector_2_out;
  wire [12:0] bitselector_1_out;

  BitSelector #(.group(13), .width(24)) bitselector_1 (.in(IR_input), .out(bitselector_1_out), .sel(1'b1));
  BitSelector #(.group(6), .width(13)) bitselector_2 (.in(bitselector_1_out), .out(bitselector_2_out), .sel(2'b01));
  BitSelector #(.group(3), .width(13)) bitselector_3 (.in(bitselector_1_out), .out(Register1), .sel(3'b001));
  BitSelector #(.group(3), .width(13)) bitselector_4 (.in(bitselector_1_out), .out(Register2), .sel(3'b000));
  BitSelector #(.group(16), .width(24)) bitselector_5 (.in(IR_input), .out(Liter), .sel(1'b0));
  BitSelector #(.group(5), .width(6)) bitselector_6 (.in(bitselector_2_out), .out(OP_code), .sel(1'b0));
endmodule

module ALU (
  input  [15:0] INPUT_1,
  input  [15:0] INPUT_2,
  input  CLOCK,
  input  [7:0] OP_CODE,
  output [15:0] ALU_OUT,
  output GR_FLAG,
  output EQ_FLAG,
  output SM_FLAG
);

  wire comparator_1_eq, comparator_1_gt, comparator_1_lt, comparator_2_eq, comparator_2_gt, comparator_2_lt,
       IS_SIGNED_out, multiplexer_1_out, multiplexer_2_out, multiplexer_3_out;
  wire [2:0] bitselector_1_out;
  wire [3:0] bit_extender_1_out;
  wire [7:0] OP_CODE_t;
  wire [15:0] adder_1_out, divider_1_out, multiplier_1_out, shifter_1_out, shifter_2_out, subtractor_1_out;

  Comparator #(.mode("unsigned"), .width(16)) comparator_1 (
    .a(INPUT_1), .b(INPUT_2), .gt(comparator_1_gt), .eq(comparator_1_eq), .lt(comparator_1_lt));
  Comparator #(.width(16)) comparator_2 (
    .a(INPUT_1), .b(INPUT_2), .gt(comparator_2_gt), .eq(comparator_2_eq), .lt(comparator_2_lt));
  PLA #(.in_width(8), .out_width(1), .\table ("00011000 1 # CMP\n00011001 0")) IS_SIGNED (
    .in(OP_CODE), .out(IS_SIGNED_out));
  Adder #(.width(16)) adder_1 (.a(INPUT_1), .b(INPUT_2), .out(adder_1_out));  // open: cin, cout
  Subtractor #(.width(16)) subtractor_1 (.a(INPUT_1), .b(INPUT_2), .out(subtractor_1_out));  // open: bin, bout
  Multiplier #(.width(16)) multiplier_1 (.a(INPUT_1), .b(INPUT_2), .out(multiplier_1_out));  // open: cin, cout
  Divider #(.width(16)) divider_1 (.a(INPUT_1), .b(INPUT_2), .out(divider_1_out));  // open: upper, rem
  Bit_Extender #(.in_width(16), .out_width(4)) bit_extender_1 (.in(INPUT_2), .out(bit_extender_1_out));
  Multiplexer multiplexer_1 (
    .in0(comparator_1_gt), .in1(comparator_2_gt), .out(multiplexer_1_out), .sel(IS_SIGNED_out));
  Multiplexer multiplexer_2 (
    .in0(comparator_1_eq), .in1(comparator_2_eq), .out(multiplexer_2_out), .sel(IS_SIGNED_out));
  Multiplexer multiplexer_3 (
    .in0(comparator_1_lt), .in1(comparator_2_lt), .out(multiplexer_3_out), .sel(IS_SIGNED_out));
  Shifter #(.width(16)) shifter_1 (.in(INPUT_1), .\dist (bit_extender_1_out), .out(shifter_1_out));
  Shifter #(.shift("lr"), .width(16)) shifter_2 (.in(INPUT_1), .\dist (bit_extender_1_out), .out(shifter_2_out));
  Register #(.width(1)) register_1 (.D(multiplexer_1_out), .clk(CLOCK), .Q(GR_FLAG));  // open: en, clr
  Register #(.width(1)) register_2 (.D(multiplexer_2_out), .clk(CLOCK), .Q(EQ_FLAG));  // open: en, clr
  Register #(.width(1)) register_3 (.D(multiplexer_3_out), .clk(CLOCK), .Q(SM_FLAG));  // open: en, clr
  Multiplexer #(.select(3), .width(16)) multiplexer_4 (
    .in0(adder_1_out), .in1(subtractor_1_out), .in2(multiplier_1_out), .in3(divider_1_out),
    .in4(shifter_1_out), .in5(shifter_2_out), .out(ALU_OUT), .sel(bitselector_1_out));  // open: in6, in7
  BitSelector #(.group(3)) bitselector_1 (.in(OP_CODE_t), .out(bitselector_1_out), .sel(2'b00));
endmodule

module Control (
  input  [7:0] OP_CODE,
  input  CLOCK
);

  wire or_1_out, or_2_out, RESET, STAGE_EXECUTE, STAGE_FETCH, STAGE_REG, USE_ALU_OUTPUT, USE_MEM_OUTPUT,
       WRITE_MEM, WRITE_REG;

  Pull_Resistor pull_resistor_1 (.node(RESET));
  or or_1 (or_1_out, RESET, STAGE_EXECUTE);
  Register #(.width(1)) register_1 (.D(or_1_out), .en(1'b1), .clk(or_2_out), .Q(STAGE_FETCH));  // open: clr
  or or_2 (or_2_out, CLOCK, RESET);
  PLA #(.in_width(8), .out_width(1), .\table ("00000010 1 # move instruction")) pla_1 (.in(OP_CODE), .out(WRITE_REG));
  PLA #(.in_width(8), .out_width(1), .\table ("00000011 1 # store instruction")) pla_2 (.in(OP_CODE), .out(WRITE_MEM));
  PLA #(.in_width(8), .out_width(1), .\table ("00000100 1 # load instruction")) pla_3 (
    .in(OP_CODE), .out(USE_MEM_OUTPUT));
  PLA pla_4 (.in(OP_CODE), .out(USE_ALU_OUTPUT));
  Register #(.width(1)) register_2 (.D(STAGE_FETCH), .en(1'b1), .clk(or_2_out), .Q(STAGE_REG), .clr(RESET));
  Register #(.width(1)) register_3 (.D(STAGE_REG), .en(1'b1), .clk(or_2_out), .Q(STAGE_EXECUTE), .clr(RESET));
endmodule

module ROMConverter (
  input  [23:0] D1,
  input  [23:0] D2,
  input  [23:0] D3,
  input  [23:0] D4,
  output [23:0] INST
);

  wire [23:0] or_1_out, or_2_out, shifter_1_out, shifter_2_out, shifter_3_out;

  Shifter #(.width(24)) shifter_1 (.in(D1), .\dist (5'b01100), .out(shifter_1_out));
  Shifter #(.width(24)) shifter_2 (.in(D2), .\dist (5'b00100), .out(shifter_2_out));
  Shifter #(.width(24)) shifter_3 (.in(D3), .\dist ({5{1'b0}}), .out(shifter_3_out));
  assign or_1_out = shifter_1_out | shifter_2_out;  // OR_Gate or_1, 24 bits wide
  assign or_2_out = shifter_3_out | D4;  // OR_Gate or_2, 24 bits wide
  assign INST = or_1_out | or_2_out;  // OR_Gate or_3, 24 bits wide
endmodule

module IRDecoder (
  input  [15:0] INST,
  output [7:0] OP_CODE,
  output [2:0] REG1,
  output [2:0] REG2,
  output LIT_FLAG
);

  wire [7:0] bitselector_1_out, shifter_1_out;

  BitSelector #(.group(8), .width(16)) bitselector_1 (.in(INST), .out(bitselector_1_out), .sel(1'b0));
  BitSelector #(.group(8), .width(16)) bitselector_2 (.in(INST), .out(OP_CODE), .sel(1'b1));
  BitSelector #(.width(16)) bitselector_3 (.in(INST), .out(LIT_FLAG), .sel(4'b0001));
  Shifter #(.shift("lr")) shifter_1 (.in(bitselector_1_out), .\dist (3'b010), .out(shifter_1_out));
  BitSelector #(.group(3)) bitselector_4 (.in(shifter_1_out), .out(REG1), .sel(2'b01));
  BitSelector #(.group(3)) bitselector_5 (.in(shifter_1_out), .out(REG2), .sel(2'b00));
endmodule

module CMPFlagSelector (
  input  GR_FLAG,
  input  EQ_FLAG,
  input  SM_FLAG,
  input  [7:0] OP_CODE,
  output FLAG
);

  wire not_1_out;
  wire [2:0] bitselector_1_out;

  not not_1 (not_1_out, EQ_FLAG);
  BitSelector #(.group(3)) bitselector_1 (.in(OP_CODE), .out(bitselector_1_out), .sel(2'b00));
  Multiplexer #(.select(3)) multiplexer_1 (
    .in0(1'b1), .in1(EQ_FLAG), .in2(not_1_out), .in3(GR_FLAG), .in4(SM_FLAG), .out(FLAG),
    .sel(bitselector_1_out));  // open: in5, in6, in7
endmodule
